// Logisim project Lab3_P2_HecDecode.circ as structural Verilog: 1 circuit, main circuit main
module main (
  input  A,
  input  B,
  input  C,
  input  D
);

  wire a_out, A_prime_B_prime_C_prime_D_out, A_prime_B_prime_out, A_prime_BD_out, A_prime_C_out,
       A_prime_C_prime_D_prime_out, A_prime_CD_out, AB_prime_C_prime_out, AC_prime_D_out, AD_prime_out,
       b_out, B_prime_D_prime_out, BC_out, c_out, C_prime_D_out, not_1_out, not_2_out, not_3_out, not_4_out,
       undriven, undriven_2, undriven_3, undriven_4;

  not not_1 (not_1_out, A);
  not not_2 (not_2_out, C);
  not not_3 (not_3_out, B);
  not not_4 (not_4_out, D);
  and B_prime_D_prime (B_prime_D_prime_out, not_3_out, not_4_out);
  and A_prime_C (A_prime_C_out, not_1_out, C);
  and BC (BC_out, B, C);
  and AD_prime (AD_prime_out, A, not_4_out);
  and A_prime_BD (A_prime_BD_out, not_1_out, B, D);
  and AB_prime_C_prime (AB_prime_C_prime_out, A, not_3_out, not_2_out);
  and A_prime_B_prime (A_prime_B_prime_out, not_1_out, not_3_out);
  and A_prime_C_prime_D_prime (A_prime_C_prime_D_prime_out, not_1_out, not_2_out, not_4_out);
  and AC_prime_D (AC_prime_D_out, A, not_2_out, D);
  and A_prime_CD (A_prime_CD_out, not_1_out, C, D);
  or C_prime_D (C_prime_D_out, not_2_out, D);
  and A_prime_B_prime_C_prime_D (A_prime_B_prime_C_prime_D_out, A_prime_B_prime_out, C_prime_D_out);
  or u_a (a_out, B_prime_D_prime_out, A_prime_C_out, BC_out, AD_prime_out, A_prime_BD_out, AB_prime_C_prime_out);
  or u_b (b_out, B_prime_D_prime_out, A_prime_B_prime_out, A_prime_C_prime_D_prime_out, AC_prime_D_out, A_prime_CD_out);
  or u_c (c_out, AC_prime_D_out, A_prime_B_prime_C_prime_D_out);
  _7_Segment_Display u_7_segment_display_1 (
    .g(undriven_2), .f(undriven), .a(a_out), .b(b_out), .e(undriven_3), .d(undriven_4), .c(c_out));  // open: dp

  // Notes on the sheet:
  //   A
  //   B
  //   -A
  //   C
  //   -C
  //   -B
  //   D
  //   -D
  //   a
  //   b
  //   c
  //   D
  //   E
  //   F
  //   G
endmodule
