// Logisim project Lab6_P1_FordThunderbird.circ as structural Verilog: 1 circuit, main circuit main
module main (
  input  L,
  input  R,
  input  H,
  output out_4,
  output out_5,
  output out_6,
  output out_7,
  output out_8,
  output out_9
);

  wire and_1_out, and_2_out, and_3_out, and_4_out, and_5_out, and_6_out, and_7_out, clock_1_out, D1_out,
       D2_out, d_ff_1_q, d_ff_1_qn, d_ff_2_q, d_ff_2_qn, I_out, or_1_out, or_2_out, Q1_prime_Q2I_out,
       Q1Q2_prime_I_out;

  or I (I_out, L, H, R);
  and and_1 (and_1_out, d_ff_2_q, H);
  or LC (out_4, and_1_out, and_2_out);
  and and_2 (and_2_out, d_ff_1_q, d_ff_2_q, L);
  or LB (out_5, and_1_out, and_3_out);
  and Q1Q2_prime_I (Q1Q2_prime_I_out, I_out, d_ff_2_qn, d_ff_1_q);
  and Q1_prime_Q2I (Q1_prime_Q2I_out, I_out, d_ff_1_qn, d_ff_2_q);
  and and_3 (and_3_out, d_ff_1_q, L);
  Clock clock_1 (.out(clock_1_out));
  or D1 (D1_out, Q1Q2_prime_I_out, Q1_prime_Q2I_out);
  and D2 (D2_out, I_out, d_ff_2_qn);
  or or_1 (or_1_out, d_ff_2_q, d_ff_1_q);
  and and_4 (and_4_out, L, or_1_out);
  or LA (out_6, and_1_out, and_4_out);
  D_Flip_Flop d_ff_1 (.clk(clock_1_out), .D(D1_out), .Q(d_ff_1_q), .Qn(d_ff_1_qn));  // open: preset, en, reset
  D_Flip_Flop d_ff_2 (.clk(clock_1_out), .D(D2_out), .Q(d_ff_2_q), .Qn(d_ff_2_qn));  // open: preset, en, reset
  or or_2 (or_2_out, d_ff_2_q, d_ff_1_q);
  and and_5 (and_5_out, or_2_out, R);
  or RA (out_7, and_1_out, and_5_out);
  and and_6 (and_6_out, d_ff_1_q, R);
  or RB (out_8, and_1_out, and_6_out);
  or RC (out_9, and_1_out, and_7_out);
  and and_7 (and_7_out, d_ff_2_q, d_ff_1_q, R);

  // Notes on the sheet:
  //   Q1
  //   Q2
  //   L
  //   R
endmodule
